# Fritzing sketch FritzingSketch (saved by Fritzing 0.9.3b)
circuit board: 8.46667cm x 5.64444cm
stripboards: 1

parts:
  R5 = Resistor [tolerance=±5% resistance=1k package=THT]
  BC546 = NPN-Transistor [package="TO92 [THT]"]
  TWI2-SDA = Generic female header - 1 pin [form="♀ (female)" package=THT]
  GND = Generic female header - 1 pin [form="♀ (female)" package=THT]
  VCC-5V = Generic female header - 1 pin [form="♀ (female)" package=THT]
  Arduino = My Arduino Pro Mini
  VCC-3V3 = Generic female header - 1 pin [form="♀ (female)" package=THT]
  R6 = Resistor [tolerance=±5% resistance=47 package=THT]
  TWI2-SCK = female alternating pin header, 1 pin [form="♀ (female)"]
  IR_LED1 = LTE-302 [package=lte-302]
  IR_LED_2 = LTE-302 [package=lte-302]  # not connected

nets:
  N1: R5.Pin_0, BC546.B
  N2: R5.Pin_1, Arduino.D3
  N3: BC546.E, GND.pin1, Arduino.GND
  N4: BC546.C, R6.Pin_1
  N5: TWI2-SDA.pin1, Arduino.A4
  N6: VCC-5V.pin1, IR_LED1.A
  N7: Arduino.VCC, VCC-3V3.pin1
  N8: Arduino.A5, TWI2-SCK.pin1

custom parts:
  Generic female header - 1 pin: Generic female header
  My Arduino Pro Mini: Copied from SparkFun's one
